# Fritzing sketch CARDREGISTRATION_11.10.2018 (saved by Fritzing 0.9.3b)
breadboards: 1

parts:
  Parça1 = RFID-RC522-v2
  Parça2 = Arduino Uno (Rev3)

nets:
  N1: Parça1.SDA, Parça2.D10_PWM/SS
  N2: Parça1.SCK, Parça2.D13/SCK
  N3: Parça1.MOSI, Parça2.D11_PWM/MOSI
  N4: Parça1.MISO, Parça2.D12/MISO
  GND: Parça1.GND, Parça2.GND
  N5: Parça1.RST, Parça2.D9_PWM
  N6: Parça1.3_3V, Parça2.3V3

custom parts:
  RFID-RC522-v2: A simple China made RFID-RC522 Reader; do check the pin labels, as this is a MFRC522 based clone.
