# Fritzing sketch cardReading_17.10.2018 (saved by Fritzing 0.9.3b)
breadboards: 1

parts:
  Parça1 = RFID-RC522-v2
  Parça2 = Arduino Uno (Rev3)
  LED1 = LEDs [package=led10mm]
  LED2 = LED - 5mm [color="Red (633nm)" package="5 mm [THT]"]
  R1 = Resistor [tolerance=±5% resistance=220 package="0603 [SMD]"]
  R2 = Resistor [tolerance=±5% resistance=220 package="0603 [SMD]"]
  J1 = Piezo Speaker
  R3 = Resistor [tolerance=±5% resistance=220 package="0603 [SMD]"]
  J2 = Basic Servo

nets:
  N1: Parça1.SDA, Parça2.D10_PWM/SS
  N2: Parça1.SCK, Parça2.D13/SCK
  N3: Parça1.MOSI, Parça2.D11_PWM/MOSI
  N4: Parça1.MISO, Parça2.D12/MISO
  GND: Parça1.GND, Parça2.GND, R1.Pin_1, R2.Pin_1, R3.Pin_1, J2.gnd
  N5: Parça1.RST, Parça2.D9_PWM
  N6: Parça1.3_3V, Parça2.3V3
  N7: Parça2.D4, J2.pulse
  N8: Parça2.D5_PWM, J1.pin2
  N9: Parça2.D6_PWM, LED1.A
  N10: Parça2.D7, LED2.anode
  5V: Parça2.5V, J2.vcc
  N11: LED1.C, R1.Pin_0
  N12: LED2.cathode, R2.Pin_0
  N13: J1.pin1, R3.Pin_0

custom parts:
  RFID-RC522-v2: A simple China made RFID-RC522 Reader; do check the pin labels, as this is a MFRC522 based clone.
